// Digital circuit soc.dig as structural Verilog
module soc (
  input  clk,
  output [31:0] a0,
  output [31:0] addr,
  output [31:0] data
);

  memory #(.applicationType("IVERILOG"), .CodeFile("memory.v")) u_memory (
    .mem_addr(addr), .i_mem_data({32{1'b0}}), .mem_rw(1'b1), .clk(clk), .o_mem_data(data));
  cpu #(.applicationType("IVERILOG"), .CodeFile("cpu.v")) u_cpu (
    .mem_rdata(data), .resetn(1'b1), .clk(clk), .mem_addr(addr), .a0(a0));

  // Notes on the sheet:
  //   clk: Hz: 10
endmodule
